# Fritzing sketch Arduino_Breakout (saved by Fritzing 0.8.7b)
circuit board: 12.2455cm x 6.43691cm
breadboards: 1

parts:
  Part1 = Arduino Mega 2560 (Rev3)
  J2 = DB15F_2
  J3 = DB15F_2
  J4 = DB15F_2
  U2 = Voltage Regulator - 5V [package="TO220 [THT]"]
  J5 = MIDI_CONN_FEMALE_SUPPORT [package=din_5_female_support]
  J6 = MIDI_CONN_FEMALE_SUPPORT [package=din_5_female_support]
  R1 = Resistor [tolerance=±5% resistance=220 package=THT]
  R2 = Resistor [tolerance=±5% resistance=220 package=THT]
  R3 = Resistor [tolerance=±5% resistance=270 package=THT]
  D1 = Rectifier Diode [part_number=1N4001 package="300 mil [THT]"]
  U1 = IC, DIP package, 8 pins [chip_label=6N138]
  J7 = Power Jack [package=power_jack_pth_lock]

nets:
  GND: Part1.GND, J2.pin8, J3.pin8, J4.pin8, U2.GND, J5.NC2, U1.pin5, J7.GND, J7.GNDBREAK
  N1: Part1.D13_PWM, J2.pin12, J3.pin12, J4.pin12
  N2: Part1.D12_PWM, J2.pin13, J3.pin13, J4.pin13
  N3: Part1.D11_PWM, J2.pin5, J3.pin5, J4.pin5
  N4: Part1.D10_PWM, J2.pin4
  N5: Part1.D9_PWM, J2.pin6, J3.pin6, J4.pin6
  N6: Part1.D8_PWM, J3.pin4
  5V: Part1.VIN, J2.pin15, J3.pin15, J4.pin15, U2.output_voltage, R1.Pin_1, R3.Pin_1, U1.pin8
  N7: Part1.D0_RX0, R3.Pin_0, U1.pin6
  N8: Part1.D1_TX0, J5.MIDI_OUT
  N9: Part1.D2_PWM, J4.pin2
  N10: Part1.D3_PWM, J3.pin2
  N11: Part1.D4_PWM, J2.pin2
  N12: Part1.D5_PWM, J2.pin10, J3.pin10, J4.pin10
  N13: Part1.D6_PWM, J2.pin3, J3.pin3, J4.pin3
  N14: Part1.D7_PWM, J4.pin4
  N15: U2.input_voltage, J7.PWR
  N16: J5.MIDI_IN, R1.Pin_0
  N17: J6.MIDI_IN, R2.Pin_0
  N18: J6.MIDI_OUT, D1.anode, U1.pin3
  N19: R2.Pin_1, D1.cathode, U1.pin2

notes:
  Sequencer Breakout
  Simon Nuk
  January 2014
  MIDI Out
  MIDI In
